# Fritzing sketch Diagrama (saved by Fritzing 0.9.3b)
breadboards: 2

parts:
  Componente1 = Arduino Uno (Rev3)
  U1 = LCD-16X2 [package=lcd-16x2_noholes]
  R1 = Resistor [tolerance=±5% resistance=1k package="2010 [SMD]"]
  R2 = Resistor [tolerance=±5% resistance=220 package="2010 [SMD]"]
  U2 = ESP8266 NodeMCU LoLin module
  DHT1 = DHT11 Humitidy and Temperature Sensor
  Componente2 = Gas Sensor Breakout Board
  Componente3 = FC-28 Soil Hygrometer Module
  Componente4 = Soil Moisture Sensor
  KY-1 = Keyes Relay [package=THT]
  WATER_PUMP1 = water pump/motor
  R3 = Resistor [tolerance=±5% resistance=220 package="2010 [SMD]"]  # not connected
  R4 = Resistor [tolerance=±5% resistance=47k package="2010 [SMD]"]
  R5 = Resistor [tolerance=±5% resistance=47k package="2010 [SMD]"]  # not connected
  R6 = Resistor [tolerance=±5% resistance=47k package="2010 [SMD]"]
  BAT1 = BC9VPC [package=bc9vpc]

nets:
  N1: Componente1.D8, KY-1.signal
  N2: Componente1.D9_PWM, DHT1.NULL
  N3: Componente1.D0/RX, U2.RX
  N4: Componente1.D1/TX, U2.TX
  N5: Componente1.D2, U1.RS
  N6: Componente1.D3_PWM, U1.E
  N7: Componente1.D4, U1.DB4
  N8: Componente1.D5_PWM, U1.DB5
  N9: Componente1.D6_PWM, U1.DB6
  N10: Componente1.D7, U1.DB7
  5V: Componente1.5V, U1.VDD, R2.Pin_0, KY-1.power, R6.Pin_1
  GND: Componente1.GND, U1.VSS, U1.R_W, U1.K, R1.Pin_0, U2.GND, DHT1.GND, Componente2.GND, Componente3.GND, KY-1.ground
  N11: U1.VO, R1.Pin_1
  N12: U1.A, R2.Pin_1
  N13: U2.D1, DHT1.DATA, R4.Pin_1
  N14: U2.D2, Componente3.AO, R6.Pin_0
  3V3: U2.3V3, DHT1.VDD, Componente2.H1, Componente3.VCC
  N15: U2.D6, Componente2.A1
  N16: Componente3.POS, Componente4.VCC
  N17: Componente3.NEG, Componente4.GND
  N18: KY-1.C, BAT1.V-
  N19: KY-1.NO, WATER_PUMP1.pin_1
  N20: WATER_PUMP1.pin_2, BAT1.V+

custom parts:
  ESP8266 NodeMCU LoLin module: ESP8266 based NodeMCU
  DHT11 Humitidy and Temperature Sensor: DHT11 Humidity and Temperature Sensor
  FC-28 Soil Hygrometer Module: The FC-28 is a soil hygrometer module that uses the Texas Instruments LM393 comparator chip to provide an analog measurement of soil humidity. The digital output is high when soil moisture is over a certain threshold, as determined by adjusting the potentiometer.
  Keyes Relay: The Keyes 5V relay module is suitable for SCM development, home appliance control. It uses a 5V~12V TIL control signal which can control DC / AC signal.
  water pump/motor: WATER PUMP BY ARDUBLOCKTR
